# Fritzing sketch bbqduino (saved by Fritzing 0.9.3b)
breadboards: 2

parts:
  U1 = NodeMCU V1.0
  Composant1 = Adafruit ADS1015 12Bit I2C ADC [part_number="Adafruit #1083"]
  Composant2 = Adafruit 4-channel I2C-safe Bi-directional Logic Level Converter [part_number="Adafruit #757"]
  Power_plug1 = Power plug
  Composant3 = LCD1602-I2C
  T1 = LM35 Temperature Sensor [package="TO92 [THT]"]
  S1 = Pushbutton [package="[THT]"]
  S2 = Pushbutton [package="[THT]"]
  LED1 = LED - 3mm [color="Red (633nm)" package="3 mm [THT]"]
  R1 = Resistor [tolerance=±5% resistance=220 package=THT]
  R3 = Resistor [tolerance=±5% resistance=10k package="2512 [SMD]"]
  R4 = Resistor [tolerance=±5% resistance=22k package="2512 [SMD]"]
  R5 = Resistor [tolerance=±5% resistance=22k package="2512 [SMD]"]
  R7 = Resistor [tolerance=±5% resistance=22k package="2512 [SMD]"]
  R8 = Temperature Sensor (Thermistor) [thermistor_type=NTC package=THT]
  R9 = Temperature Sensor (Thermistor) [thermistor_type=NTC package=THT]
  R10 = Temperature Sensor (Thermistor) [thermistor_type=NTC package=THT]
  S3 = Toggle Switch [package=THT]
  R2 = Resistor [tolerance=±5% resistance=10k package="2512 [SMD]"]

nets:
  N1: U1.D0, R1.Pin_0
  N2: U1.D1, Composant1.SDA, Composant2.A4
  N3: U1.D2, Composant1.SCL, Composant2.A3
  N4: U1.D3, S1.Pin_1, S1.Pin_2, R2.Pin_0
  N5: U1.D4, S2.Pin_1, S2.Pin_2, R3.Pin_0
  3V3: U1.3V3, U1.EN, Composant1.VDD, Composant2.LV, T1.+Vs, LED1.anode, R3.Pin_1, R4.Pin_1, R5.Pin_1, R7.Pin_1, R2.Pin_1
  GND: U1.GND, Composant1.GND, Composant2.GND, Power_plug1.GND, Composant3.GND, T1.GND, S1.Pin_3, S1.Pin_4, S2.Pin_3, S2.Pin_4, R8.pin_1, R9.pin_1, R10.pin_1
  VIN: U1.Vin, Composant2.HV, Composant3.VCC, S3.L2
  N6: U1.A0, T1.Vout
  N7: Composant1.AIN2, R7.Pin_0, R10.pin_0
  N8: Composant1.AIN1, R5.Pin_0, R9.pin_0
  N9: Composant1.AIN0, R4.Pin_0, R8.pin_0
  N10: Composant2.B4, Composant3.SDA
  N11: Composant2.B3, Composant3.SCL
  N12: Power_plug1.VCC, S3.COM
  N13: LED1.cathode, R1.Pin_1

notes:
  5v from XL6019
  3.3v  nodemcu
  lcd 16x2 i2c 5v
  BbqDuino-v1-14/04/2018-nd
  level shifter

custom parts:
  NodeMCU V1.0: ESP8266 based NodeMCU
  Adafruit ADS1015 12Bit I2C ADC: For microcontrollers without an analog-to-digital converter or when you want a higher-precision ADC, the ADS1015 provides 12-bit precision at 3300 samples/second over I2C. The chip can be configured as 4 single-ended input channels, or two differential channels. As a nice bonus, it even includes a programmable gain amplifier, up to x16, to help boost up smaller single/differential signals to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
  Adafruit 4-channel I2C-safe Bi-directional Logic Level Converter: Because the Arduino (and Basic Stamp) are 5V devices, and most modern sensors, displays, flash cards and modes are 3.3V-only, many makers find that they need to perform level shifting/conversion to protect the 3.3V device from 5V. We do have some other handy level shifters in the shop, from the DIP 74LVC245 to the fancy bi-directional TXB0108. However, neither of these are happy to work with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
  LCD1602-I2C: A standard character display, usually with 2x16 characters. Comes in many colors with LCM1602 IIC attached.
